// Logisim project MCU_4bits_CC3Mb_24-1.circ as structural Verilog: 5 circuits, main circuit main
module main (
  input  in_1,
  input  in_2,
  input  [3:0] in_3,
  input  [3:0] in_4,
  input  in_5,
  input  in_6,
  input  in_7,
  input  in_8,
  input  in_9,
  input  [3:0] in_10,
  input  [3:0] in_11,
  input  in_12,
  input  in_13,
  output out_14,
  output out_15,
  output [3:0] out_16,
  output out_17,
  output out_18,
  output out_19,
  output [3:0] out_20
);

  SUB_1 sub_1_1 (.A(in_8), .B(in_9), .Vem_1(in_12), .out_4(out_19), .out_5(out_17));
  ADD_1 add_1_1 (.A(in_1), .B(in_2), .Vem_1(in_5), .out_4(out_15), .out_5(out_14));
  SUB_4 sub_4_1 (.A(in_10), .Overflow(out_18), .B(in_11), .Vem_1(in_13), .out_5(out_20));
  ADD_4 add_4_1 (.in_1(in_3), .Var_1(in_6), .in_2(in_4), .Vem_1(in_7), .out_5(out_16));
endmodule

module ADD_1 (
  input  A,
  input  B,
  input  Vem_1,
  output out_4,
  output out_5
);

  wire and_1_out, and_2_out, or_1_out, xor_1_out;

  xor xor_1 (xor_1_out, A, B);
  or or_1 (or_1_out, B, Vem_1);
  and and_1 (and_1_out, or_1_out, A);
  and and_2 (and_2_out, B, Vem_1);
  xor xor_2 (out_4, xor_1_out, Vem_1);
  or or_2 (out_5, and_1_out, and_2_out);
endmodule

module ADD_4 (
  input  [3:0] in_1,
  input  [3:0] in_2,
  input  Vem_1,
  output Var_1,
  output [3:0] out_5
);

  wire add_1_2_out_5, add_1_3_out_5, add_1_4_out_5;

  ADD_1 add_1_1 (.A(in_1[3]), .B(in_2[3]), .Vem_1(add_1_2_out_5), .out_4(out_5[3]), .out_5(Var_1));
  ADD_1 add_1_2 (.A(in_1[2]), .B(in_2[2]), .Vem_1(add_1_3_out_5), .out_4(out_5[2]), .out_5(add_1_2_out_5));
  ADD_1 add_1_3 (.A(in_1[1]), .B(in_2[1]), .Vem_1(add_1_4_out_5), .out_4(out_5[1]), .out_5(add_1_3_out_5));
  ADD_1 add_1_4 (.A(in_1[0]), .B(in_2[0]), .Vem_1(Vem_1), .out_4(out_5[0]), .out_5(add_1_4_out_5));
endmodule

module SUB_1 (
  input  A,
  input  B,
  input  Vem_1,
  output out_4,
  output out_5
);

  wire and_1_out, and_2_out, not_1_out, or_1_out, xor_1_out;

  not not_1 (not_1_out, A);
  xor xor_1 (xor_1_out, A, B);
  or or_1 (or_1_out, B, Vem_1);
  and and_1 (and_1_out, or_1_out, not_1_out);
  and and_2 (and_2_out, B, Vem_1);
  xor xor_2 (out_4, xor_1_out, Vem_1);
  or or_2 (out_5, and_1_out, and_2_out);
endmodule

module SUB_4 (
  input  [3:0] A,
  input  [3:0] B,
  input  Vem_1,
  output Overflow,
  output [3:0] out_5
);

  wire sub_1_2_out_5, sub_1_3_out_5, sub_1_4_out_5;

  SUB_1 sub_1_1 (.A(A[3]), .B(B[3]), .Vem_1(sub_1_2_out_5), .out_4(out_5[3]), .out_5(Overflow));
  SUB_1 sub_1_2 (.A(A[2]), .B(B[2]), .Vem_1(sub_1_3_out_5), .out_4(out_5[2]), .out_5(sub_1_2_out_5));
  SUB_1 sub_1_3 (.A(A[1]), .B(B[1]), .Vem_1(sub_1_4_out_5), .out_4(out_5[1]), .out_5(sub_1_3_out_5));
  SUB_1 sub_1_4 (.A(A[0]), .B(B[0]), .Vem_1(Vem_1), .out_4(out_5[0]), .out_5(sub_1_4_out_5));
endmodule
